// Logisim project sap1_2008036_auto.circ as structural Verilog: 13 circuits, main circuit main
module main (
  input  [7:0] in_1,
  input  in_2,
  input  in_3,
  input  in_4,
  input  in_5,
  input  in_6,
  input  in_7,
  input  in_8,
  input  in_9,
  input  [7:0] in_10,
  input  in_11,
  input  in_12,
  input  in_13,
  input  in_14,
  input  [7:0] in_15,
  input  in_16,
  input  in_17,
  input  [7:0] in_18,
  output [3:0] out_19,
  output [7:0] out_20,
  output [7:0] out_21,
  output [7:0] out_22,
  output [7:0] out_23,
  output out_24
);

  wire [7:0] reg_gp_1_reg_int_out, reg_gp_2_reg_int_out;

  reg_gp reg_gp_1 (
    .reg_in(in_1), .reg_in_en(in_2), .reg_clk(in_3), .reg_int_out(reg_gp_1_reg_int_out));  // open: reg_out_en, reg_out
  reg_gp reg_gp_2 (
    .reg_in(in_1), .reg_in_en(in_14), .reg_clk(in_3), .reg_int_out(reg_gp_2_reg_int_out));  // open: reg_out_en, reg_out
  alu alu_1 (
    .alu_in_1(reg_gp_1_reg_int_out), .alu_out_en(in_8), .alu_sub(in_9), .alu_in_2(reg_gp_2_reg_int_out),
    .alu_out(out_20));  // open: alu_carry_out
  reg_gp reg_gp_3 (
    .reg_in(in_10), .reg_in_en(in_11), .reg_clk(in_12), .reg_out_en(in_13), .reg_int_out(out_21),
    .reg_out(out_22));
  alu alu_2 (
    .alu_in_1(in_15), .alu_out_en(in_16), .alu_sub(in_17), .alu_in_2(in_18), .alu_out(out_23),
    .alu_carry_out(out_24));
  program_counter program_counter_1 (
    .pc_en(in_4), .pc_clk(in_5), .pc_reset(in_6), .pc_out_en(in_7), .pc_value(out_19));  // open: pc_out
endmodule

module reg_gp (
  input  [7:0] reg_in,
  input  reg_in_en,
  input  reg_clk,
  input  reg_out_en,
  output [7:0] reg_int_out,
  output [7:0] reg_out
);

  wire multiplexer_1_out, multiplexer_2_out, multiplexer_3_out, multiplexer_4_out, multiplexer_5_out,
       multiplexer_6_out, multiplexer_7_out, multiplexer_8_out;

  Multiplexer multiplexer_1 (.in0(reg_int_out[7]), .in1(reg_in[7]), .out(multiplexer_1_out), .sel(reg_in_en));
  D_Flip_Flop d_ff_1 (.D(multiplexer_1_out), .clk(reg_clk), .Q(reg_int_out[7]));  // open: Qn, preset, reset
  Multiplexer multiplexer_2 (.in0(reg_int_out[6]), .in1(reg_in[6]), .out(multiplexer_2_out), .sel(reg_in_en));
  assign reg_out[7] = reg_out_en ? reg_int_out[7] : 1'bz;  // Controlled_Buffer controlled_buffer_1
  D_Flip_Flop d_ff_2 (.D(multiplexer_2_out), .clk(reg_clk), .Q(reg_int_out[6]));  // open: Qn, preset, reset
  Multiplexer multiplexer_3 (.in0(reg_int_out[5]), .in1(reg_in[5]), .out(multiplexer_3_out), .sel(reg_in_en));
  assign reg_out[6] = reg_out_en ? reg_int_out[6] : 1'bz;  // Controlled_Buffer controlled_buffer_2
  D_Flip_Flop d_ff_3 (.D(multiplexer_3_out), .clk(reg_clk), .Q(reg_int_out[5]));  // open: Qn, preset, reset
  Multiplexer multiplexer_4 (.in0(reg_int_out[4]), .in1(reg_in[4]), .out(multiplexer_4_out), .sel(reg_in_en));
  assign reg_out[5] = reg_out_en ? reg_int_out[5] : 1'bz;  // Controlled_Buffer controlled_buffer_3
  D_Flip_Flop d_ff_4 (.D(multiplexer_4_out), .clk(reg_clk), .Q(reg_int_out[4]));  // open: Qn, preset, reset
  assign reg_out[4] = reg_out_en ? reg_int_out[4] : 1'bz;  // Controlled_Buffer controlled_buffer_4
  Multiplexer multiplexer_5 (.in0(reg_int_out[3]), .in1(reg_in[3]), .out(multiplexer_5_out), .sel(reg_in_en));
  D_Flip_Flop d_ff_5 (.D(multiplexer_5_out), .clk(reg_clk), .Q(reg_int_out[3]));  // open: Qn, preset, reset
  assign reg_out[3] = reg_out_en ? reg_int_out[3] : 1'bz;  // Controlled_Buffer controlled_buffer_5
  Multiplexer multiplexer_6 (.in0(reg_int_out[2]), .in1(reg_in[2]), .out(multiplexer_6_out), .sel(reg_in_en));
  D_Flip_Flop d_ff_6 (.D(multiplexer_6_out), .clk(reg_clk), .Q(reg_int_out[2]));  // open: Qn, preset, reset
  assign reg_out[2] = reg_out_en ? reg_int_out[2] : 1'bz;  // Controlled_Buffer controlled_buffer_6
  Multiplexer multiplexer_7 (.in0(reg_int_out[1]), .in1(reg_in[1]), .out(multiplexer_7_out), .sel(reg_in_en));
  D_Flip_Flop d_ff_7 (.D(multiplexer_7_out), .clk(reg_clk), .Q(reg_int_out[1]));  // open: Qn, preset, reset
  Multiplexer multiplexer_8 (.in0(reg_int_out[0]), .in1(reg_in[0]), .out(multiplexer_8_out), .sel(reg_in_en));
  assign reg_out[1] = reg_out_en ? reg_int_out[1] : 1'bz;  // Controlled_Buffer controlled_buffer_7
  D_Flip_Flop d_ff_8 (.D(multiplexer_8_out), .clk(reg_clk), .Q(reg_int_out[0]));  // open: Qn, preset, reset
  assign reg_out[0] = reg_out_en ? reg_int_out[0] : 1'bz;  // Controlled_Buffer controlled_buffer_8
endmodule

module alu (
  input  [7:0] alu_in_1,
  input  alu_out_en,
  input  alu_sub,
  input  [7:0] alu_in_2,
  output [7:0] alu_out,
  output alu_carry_out
);

  wire adder_2_cout, adder_3_cout, adder_4_cout, adder_5_cout, adder_6_cout, adder_7_cout, adder_8_cout,
       xor_1_out, xor_2_out, xor_3_out, xor_4_out, xor_5_out, xor_6_out, xor_7_out, xor_8_out;
  wire [7:0] adder_8_out;

  xor xor_1 (xor_1_out, alu_in_2[7], alu_sub);
  Adder #(.width(1)) adder_1 (
    .a(alu_in_1[7]), .b(xor_1_out), .out(adder_8_out[7]), .cin(adder_2_cout), .cout(alu_carry_out));
  xor xor_2 (xor_2_out, alu_in_2[6], alu_sub);
  Adder #(.width(1)) adder_2 (
    .a(alu_in_1[6]), .b(xor_2_out), .out(adder_8_out[6]), .cin(adder_3_cout), .cout(adder_2_cout));
  xor xor_3 (xor_3_out, alu_in_2[5], alu_sub);
  Adder #(.width(1)) adder_3 (
    .a(alu_in_1[5]), .b(xor_3_out), .out(adder_8_out[5]), .cin(adder_4_cout), .cout(adder_3_cout));
  xor xor_4 (xor_4_out, alu_in_2[4], alu_sub);
  Adder #(.width(1)) adder_4 (
    .a(alu_in_1[4]), .b(xor_4_out), .out(adder_8_out[4]), .cin(adder_5_cout), .cout(adder_4_cout));
  xor xor_5 (xor_5_out, alu_in_2[3], alu_sub);
  Adder #(.width(1)) adder_5 (
    .a(alu_in_1[3]), .b(xor_5_out), .out(adder_8_out[3]), .cin(adder_6_cout), .cout(adder_5_cout));
  xor xor_6 (xor_6_out, alu_in_2[2], alu_sub);
  Adder #(.width(1)) adder_6 (
    .a(alu_in_1[2]), .b(xor_6_out), .out(adder_8_out[2]), .cin(adder_7_cout), .cout(adder_6_cout));
  xor xor_7 (xor_7_out, alu_in_2[1], alu_sub);
  Adder #(.width(1)) adder_7 (
    .a(alu_in_1[1]), .b(xor_7_out), .out(adder_8_out[1]), .cin(adder_8_cout), .cout(adder_7_cout));
  xor xor_8 (xor_8_out, alu_in_2[0], alu_sub);
  Adder #(.width(1)) adder_8 (.a(alu_in_1[0]), .b(xor_8_out), .out(adder_8_out[0]), .cin(alu_sub), .cout(adder_8_cout));
  assign alu_out = alu_out_en ? adder_8_out : 8'bz;  // Controlled_Buffer controlled_buffer_1
endmodule

module program_counter (
  input  pc_en,
  input  pc_clk,
  input  pc_reset,
  input  pc_out_en,
  output [3:0] pc_value,
  output [3:0] pc_out
);

  wire j_k_ff_2_qn, j_k_ff_3_qn, j_k_ff_4_qn;

  J_K_Flip_Flop j_k_ff_1 (
    .J(pc_en), .K(pc_en), .clk(j_k_ff_2_qn), .Q(pc_value[3]), .reset(pc_reset));  // open: Qn, preset
  J_K_Flip_Flop j_k_ff_2 (
    .J(pc_en), .K(pc_en), .clk(j_k_ff_3_qn), .Q(pc_value[2]), .Qn(j_k_ff_2_qn), .reset(pc_reset));  // open: preset
  J_K_Flip_Flop j_k_ff_3 (
    .J(pc_en), .K(pc_en), .clk(j_k_ff_4_qn), .Q(pc_value[1]), .Qn(j_k_ff_3_qn), .reset(pc_reset));  // open: preset
  J_K_Flip_Flop j_k_ff_4 (
    .J(pc_en), .K(pc_en), .clk(pc_clk), .Q(pc_value[0]), .Qn(j_k_ff_4_qn), .reset(pc_reset));  // open: preset
  assign pc_out = pc_out_en ? pc_value : 4'bz;  // Controlled_Buffer controlled_buffer_1
endmodule

module dec (
  input  [3:0] dec_sel,
  output [15:0] dec_out
);

  wire not_1_out, not_2_out, not_3_out, not_4_out;

  not not_1 (not_1_out, dec_sel[3]);
  not not_2 (not_2_out, dec_sel[2]);
  not not_3 (not_3_out, dec_sel[1]);
  not not_4 (not_4_out, dec_sel[0]);
  and and_1 (dec_out[0], not_4_out, not_3_out, not_2_out, not_1_out);
  and and_2 (dec_out[1], dec_sel[0], not_3_out, not_2_out, not_1_out);
  and and_3 (dec_out[2], not_4_out, dec_sel[1], not_2_out, not_1_out);
  and and_4 (dec_out[3], dec_sel[0], dec_sel[1], not_2_out, not_1_out);
  and and_5 (dec_out[4], not_4_out, not_3_out, dec_sel[2], not_1_out);
  and and_6 (dec_out[5], dec_sel[0], not_3_out, dec_sel[2], not_1_out);
  and and_7 (dec_out[6], not_4_out, dec_sel[1], dec_sel[2], not_1_out);
  and and_8 (dec_out[7], dec_sel[0], dec_sel[1], dec_sel[2], not_1_out);
  and and_9 (dec_out[8], not_4_out, not_3_out, not_2_out, dec_sel[3]);
  and and_10 (dec_out[9], dec_sel[0], not_3_out, not_2_out, dec_sel[3]);
  and and_11 (dec_out[10], not_4_out, dec_sel[1], not_2_out, dec_sel[3]);
  and and_12 (dec_out[11], dec_sel[0], dec_sel[1], not_2_out, dec_sel[3]);
  and and_13 (dec_out[12], not_4_out, not_3_out, dec_sel[2], dec_sel[3]);
  and and_14 (dec_out[13], dec_sel[0], not_3_out, dec_sel[2], dec_sel[3]);
  and and_15 (dec_out[14], not_4_out, dec_sel[1], dec_sel[2], dec_sel[3]);
  and and_16 (dec_out[15], dec_sel[0], dec_sel[1], dec_sel[2], dec_sel[3]);
endmodule

module sram_cell (
  input  [7:0] data_in,
  input  wr_en,
  input  clk,
  input  cs,
  input  rd_en,
  output [7:0] memory_content,
  output [7:0] data_out
);

  wire and_1_out, and_2_out;

  and and_1 (and_1_out, wr_en, cs);
  and and_2 (and_2_out, cs, rd_en);
  reg_gp reg_gp_1 (
    .reg_in(data_in), .reg_in_en(and_1_out), .reg_clk(clk), .reg_out_en(and_2_out),
    .reg_int_out(memory_content), .reg_out(data_out));
endmodule

module sram (
  input  sram_rd,
  input  sram_wr,
  input  [7:0] sram_d_in,
  input  [7:0] mar_d_in,
  input  mar_in_en,
  input  sram_clk,
  output [7:0] sram_d_out,
  output [7:0] out_8,
  output [7:0] out_9,
  output [7:0] out_10,
  output [7:0] out_11,
  output [7:0] out_12,
  output [7:0] out_13,
  output [7:0] out_14,
  output [7:0] out_15,
  output [7:0] out_16,
  output [7:0] out_17,
  output [7:0] out_18,
  output [7:0] out_19,
  output [7:0] out_20,
  output [7:0] out_21,
  output [7:0] out_22,
  output [7:0] out_23
);

  wire [7:0] controlled_buffer_1_out, reg_gp_1_reg_int_out;
  wire [15:0] dec_1_dec_out;

  reg_gp reg_gp_1 (
    .reg_in(mar_d_in), .reg_in_en(mar_in_en), .reg_clk(sram_clk), .reg_int_out(reg_gp_1_reg_int_out));  // open: reg_out_en, reg_out
  dec dec_1 (.dec_sel(reg_gp_1_reg_int_out[3:0]), .dec_out(dec_1_dec_out));
  assign controlled_buffer_1_out = sram_wr ? sram_d_in : 8'bz;  // Controlled_Buffer controlled_buffer_1
  sram_cell sram_cell_1 (
    .data_in(controlled_buffer_1_out), .wr_en(sram_wr), .clk(sram_clk), .cs(dec_1_dec_out[0]),
    .rd_en(sram_rd), .memory_content(out_8), .data_out(controlled_buffer_1_out));
  sram_cell sram_cell_2 (
    .data_in(controlled_buffer_1_out), .wr_en(sram_wr), .clk(sram_clk), .cs(dec_1_dec_out[1]),
    .rd_en(sram_rd), .memory_content(out_9), .data_out(controlled_buffer_1_out));
  sram_cell sram_cell_3 (
    .data_in(controlled_buffer_1_out), .wr_en(sram_wr), .clk(sram_clk), .cs(dec_1_dec_out[2]),
    .rd_en(sram_rd), .memory_content(out_10), .data_out(controlled_buffer_1_out));
  sram_cell sram_cell_4 (
    .data_in(controlled_buffer_1_out), .wr_en(sram_wr), .clk(sram_clk), .cs(dec_1_dec_out[3]),
    .rd_en(sram_rd), .memory_content(out_11), .data_out(controlled_buffer_1_out));
  sram_cell sram_cell_5 (
    .data_in(controlled_buffer_1_out), .wr_en(sram_wr), .clk(sram_clk), .cs(dec_1_dec_out[4]),
    .rd_en(sram_rd), .memory_content(out_12), .data_out(controlled_buffer_1_out));
  sram_cell sram_cell_6 (
    .data_in(controlled_buffer_1_out), .wr_en(sram_wr), .clk(sram_clk), .cs(dec_1_dec_out[5]),
    .rd_en(sram_rd), .memory_content(out_13), .data_out(controlled_buffer_1_out));
  sram_cell sram_cell_7 (
    .data_in(controlled_buffer_1_out), .wr_en(sram_wr), .clk(sram_clk), .cs(dec_1_dec_out[6]),
    .rd_en(sram_rd), .memory_content(out_14), .data_out(controlled_buffer_1_out));
  sram_cell sram_cell_8 (
    .data_in(controlled_buffer_1_out), .wr_en(sram_wr), .clk(sram_clk), .cs(dec_1_dec_out[7]),
    .rd_en(sram_rd), .memory_content(out_15), .data_out(controlled_buffer_1_out));
  sram_cell sram_cell_9 (
    .data_in(controlled_buffer_1_out), .wr_en(sram_wr), .clk(sram_clk), .cs(dec_1_dec_out[8]),
    .rd_en(sram_rd), .memory_content(out_16), .data_out(controlled_buffer_1_out));
  sram_cell sram_cell_10 (
    .data_in(controlled_buffer_1_out), .wr_en(sram_wr), .clk(sram_clk), .cs(dec_1_dec_out[9]),
    .rd_en(sram_rd), .memory_content(out_17), .data_out(controlled_buffer_1_out));
  sram_cell sram_cell_11 (
    .data_in(controlled_buffer_1_out), .wr_en(sram_wr), .clk(sram_clk), .cs(dec_1_dec_out[10]),
    .rd_en(sram_rd), .memory_content(out_18), .data_out(controlled_buffer_1_out));
  sram_cell sram_cell_12 (
    .data_in(controlled_buffer_1_out), .wr_en(sram_wr), .clk(sram_clk), .cs(dec_1_dec_out[11]),
    .rd_en(sram_rd), .memory_content(out_19), .data_out(controlled_buffer_1_out));
  sram_cell sram_cell_13 (
    .data_in(controlled_buffer_1_out), .wr_en(sram_wr), .clk(sram_clk), .cs(dec_1_dec_out[12]),
    .rd_en(sram_rd), .memory_content(out_20), .data_out(controlled_buffer_1_out));
  sram_cell sram_cell_14 (
    .data_in(controlled_buffer_1_out), .wr_en(sram_wr), .clk(sram_clk), .cs(dec_1_dec_out[13]),
    .rd_en(sram_rd), .memory_content(out_21), .data_out(controlled_buffer_1_out));
  sram_cell sram_cell_15 (
    .data_in(controlled_buffer_1_out), .wr_en(sram_wr), .clk(sram_clk), .cs(dec_1_dec_out[14]),
    .rd_en(sram_rd), .memory_content(out_22), .data_out(controlled_buffer_1_out));
  sram_cell sram_cell_16 (
    .data_in(controlled_buffer_1_out), .wr_en(sram_wr), .clk(sram_clk), .cs(dec_1_dec_out[15]),
    .rd_en(sram_rd), .memory_content(out_23), .data_out(controlled_buffer_1_out));
  assign sram_d_out = sram_rd ? controlled_buffer_1_out : 8'bz;  // Controlled_Buffer controlled_buffer_2
endmodule

module ins_reg (
  input  [7:0] ins_reg_in,
  input  ins_reg_in_en,
  input  clk,
  input  ins_reg_out_en,
  output [3:0] adds_out,
  output [3:0] ins_out
);

  wire [3:0] reg_gp_1_reg_int_out;

  reg_gp reg_gp_1 (
    .reg_in(ins_reg_in), .reg_in_en(ins_reg_in_en), .reg_clk(clk),
    .reg_int_out({ins_out, reg_gp_1_reg_int_out}));  // open: reg_out_en, reg_out
  assign adds_out = ins_reg_out_en ? reg_gp_1_reg_int_out : 4'bz;  // Controlled_Buffer controlled_buffer_1
endmodule

module final_layout_lab2 (
  input  in_1,
  input  in_2,
  input  debug,
  input  pc_reset,
  input  clk,
  output [3:0] out_6,
  output [7:0] out_7,
  output out_8,
  output [7:0] out_9,
  output [7:0] out_10,
  output [7:0] out_11,
  output [7:0] out_12,
  output [7:0] out_13,
  output [7:0] out_14,
  output [7:0] out_15,
  output [7:0] out_16,
  output [7:0] out_17,
  output [7:0] out_18,
  output [7:0] out_19,
  output [7:0] out_20,
  output [7:0] out_21,
  output [7:0] out_22,
  output [7:0] out_23,
  output [7:0] out_24,
  output [7:0] out_25,
  output [7:0] out_26,
  output [3:0] out_27,
  output [3:0] out_28,
  output [7:0] out_29,
  output [3:0] out_30
);

  wire a_in, a_out, alu_out, alu_sub, b_in, ins_reg_in_en, ins_reg_out_en, l1, l2, mar_in_en, not_1_out,
       pc_en, pc_in, pc_out, sram_rd, sram_wr, undriven_2;
  wire [7:0] debug_data, multiplexer_1_out, reg_gp_1_reg_out;
  wire [7:4] undriven;

  Multiplexer #(.width(8)) multiplexer_1 (.in0(out_9), .in1({undriven, out_30}), .out(multiplexer_1_out), .sel(debug));
  not not_1 (not_1_out, clk);
  program_counter program_counter_1 (
    .pc_en(pc_en), .pc_clk(clk), .pc_reset(pc_reset), .pc_out_en(pc_out), .pc_value(out_6),
    .pc_out(out_9[3:0]));
  sram sram_1 (
    .sram_rd(sram_rd), .sram_wr(sram_wr), .sram_d_in(out_9), .mar_d_in(multiplexer_1_out),
    .mar_in_en(mar_in_en), .sram_clk(not_1_out), .sram_d_out(out_9), .out_8(out_10), .out_9(out_11),
    .out_10(out_12), .out_11(out_13), .out_12(out_14), .out_13(out_15), .out_14(out_17), .out_15(out_18),
    .out_16(out_19), .out_17(out_20), .out_18(out_21), .out_19(out_22), .out_20(out_23), .out_21(out_24),
    .out_22(out_25), .out_23(out_26));
  assign out_9 = debug ? debug_data : 8'bz;  // Controlled_Buffer controlled_buffer_1
  Hex_Digit_Display hex_digit_display_1 (.value(out_30));  // open: dp
  ins_loader ins_loader_1 (
    .bc_reset(pc_reset), .bc_en(l2), .clk(clk), .debug(debug), .bc_address(out_30), .l1(l1), .l2(l2));
  ROM #(.addrWidth(4)) rom_1 (.addr(out_30), .data(debug_data));
  reg_gp reg_gp_1 (
    .reg_in(out_9), .reg_in_en(a_in), .reg_clk(clk), .reg_out_en(a_out), .reg_int_out(out_7),
    .reg_out(reg_gp_1_reg_out));
  reg_gp reg_gp_2 (
    .reg_in(out_9), .reg_in_en(b_in), .reg_clk(clk), .reg_out_en(undriven_2), .reg_int_out(out_16),
    .reg_out(reg_gp_1_reg_out));
  ins_reg ins_reg_1 (
    .ins_reg_in(out_9), .ins_reg_in_en(ins_reg_in_en), .clk(clk), .ins_reg_out_en(ins_reg_out_en),
    .adds_out(out_9[3:0]), .ins_out(out_28));
  Hex_Digit_Display hex_digit_display_2 (.value(out_7[7:4]));  // open: dp
  Hex_Digit_Display hex_digit_display_3 (.value(out_7[3:0]));  // open: dp
  alu alu_1 (
    .alu_in_1(out_7), .alu_out_en(alu_out), .alu_sub(alu_sub), .alu_in_2(out_16), .alu_out(out_9));  // open: alu_carry_out
  Hex_Digit_Display hex_digit_display_4 (.value(out_9[7:4]));  // open: dp
  control_sequencer control_sequencer_1 (
    .clk(clk), .rc_en(in_2), .clk_reset(in_1), .ir_msb(out_28), .debug(debug), .l1(l1), .l2(l2),
    .ins_reg_in_en(ins_reg_in_en), .pc_en(pc_en), .pc_in(pc_in), .pc_out(pc_out),
    .ins_reg_out_en(ins_reg_out_en), .sram_rd(sram_rd), .b_in(b_in), .a_in(a_in), .alu_sub(alu_sub),
    .mar_in_en(mar_in_en), .a_out(a_out), .alu_out(alu_out), .sram_wr(sram_wr), .flag_in(out_8));  // open: b_out, hlt
  Hex_Digit_Display hex_digit_display_5 (.value(out_9[3:0]));  // open: dp
  Hex_Digit_Display hex_digit_display_6 (.value(out_16[7:4]));  // open: dp
  Hex_Digit_Display hex_digit_display_7 (.value(out_16[3:0]));  // open: dp

  assign out_27 = out_9[3:0];
  assign out_29 = out_9;

  // Other names for the same wires on the sheet: bc_address[3:0] = out_30; clk_reset = in_1; flag_in = out_8;
  //   rc_en = in_2

  // Notes on the sheet:
  //   contents of rom_1 (hex, n*v repeats v):
  //   17 28 40 59 e0 0 0 a 5
endmodule

module ins_dec (
  input  [3:0] ir_msb,
  output LDA,
  output LDB,
  output ADD,
  output SUB,
  output STA,
  output out_7,
  output JMP,
  output CMP,
  output HLT
);

  wire [14:0] dec_1_dec_out;

  dec dec_1 (
    .dec_sel(ir_msb),
    .dec_out({HLT, dec_1_dec_out[14:9], CMP, JMP, out_7, STA, SUB, ADD, LDB, LDA, dec_1_dec_out[0]}));
endmodule

module ring_counter (
  input  clk,
  input  rc_en,
  input  rc_reset,
  output T1,
  output T2,
  output T3,
  output T4,
  output T5,
  output T6
);

  wire and_1_out;

  and and_1 (and_1_out, clk, rc_en);
  D_Flip_Flop d_ff_1 (.D(T6), .clk(and_1_out), .Q(T1), .reset(rc_reset));  // open: Qn, preset
  D_Flip_Flop d_ff_2 (.D(T1), .clk(and_1_out), .Q(T2), .reset(rc_reset));  // open: Qn, preset
  D_Flip_Flop d_ff_3 (.D(T2), .clk(and_1_out), .Q(T3), .reset(rc_reset));  // open: Qn, preset
  D_Flip_Flop d_ff_4 (.D(T3), .clk(and_1_out), .Q(T4), .reset(rc_reset));  // open: Qn, preset
  D_Flip_Flop d_ff_5 (.D(T4), .clk(and_1_out), .Q(T5), .reset(rc_reset));  // open: Qn, preset
  D_Flip_Flop d_ff_6 (.D(T5), .clk(and_1_out), .Q(T6), .preset(rc_reset));  // open: Qn, reset
endmodule

module control_sequencer (
  input  clk,
  input  rc_en,
  input  clk_reset,
  input  [3:0] ir_msb,
  input  debug,
  input  l1,
  input  l2,
  output ins_reg_in_en,
  output pc_en,
  output pc_in,
  output pc_out,
  output ins_reg_out_en,
  output sram_rd,
  output b_out,
  output b_in,
  output a_in,
  output alu_sub,
  output mar_in_en,
  output a_out,
  output alu_out,
  output sram_wr,
  output flag_in,
  output hlt
);

  wire and_1_out, and_2_out, and_4_out, and_5_out, and_7_out, and_8_out, and_9_out, and_15_out, and_17_out,
       and_18_out, and_20_out, and_21_out, and_23_out, and_25_out, and_27_out, and_29_out, ins_dec_1_add,
       ins_dec_1_cmp, ins_dec_1_hlt, ins_dec_1_jmp, ins_dec_1_lda, ins_dec_1_ldb, ins_dec_1_sta,
       ins_dec_1_sub, not_1_out, or_2_out, or_4_out, or_5_out, or_6_out, or_7_out, or_8_out, or_9_out,
       or_10_out, or_11_out, or_12_out, or_13_out, or_14_out, ring_counter_1_t1, ring_counter_1_t2,
       ring_counter_1_t3, ring_counter_1_t4, ring_counter_1_t5, ring_counter_1_t6;

  ring_counter ring_counter_1 (
    .clk(clk), .rc_en(rc_en), .rc_reset(clk_reset), .T1(ring_counter_1_t1), .T2(ring_counter_1_t2),
    .T3(ring_counter_1_t3), .T4(ring_counter_1_t4), .T5(ring_counter_1_t5), .T6(ring_counter_1_t6));
  ins_dec ins_dec_1 (
    .ir_msb(ir_msb), .LDA(ins_dec_1_lda), .LDB(ins_dec_1_ldb), .ADD(ins_dec_1_add), .SUB(ins_dec_1_sub),
    .STA(ins_dec_1_sta), .JMP(ins_dec_1_jmp), .CMP(ins_dec_1_cmp), .HLT(ins_dec_1_hlt));  // open: out_7
  not not_1 (not_1_out, debug);
  and and_1 (and_1_out, debug, l1);
  and and_2 (and_2_out, debug, l2);
  and and_3 (a_out, not_1_out, ins_dec_1_sta, ring_counter_1_t6);
  or or_1 (sram_wr, and_2_out, and_7_out);
  or or_2 (or_2_out, ins_dec_1_cmp, ins_dec_1_ldb, ins_dec_1_lda, ins_dec_1_add, ins_dec_1_sub, ins_dec_1_sta, ins_dec_1_jmp);
  and and_4 (and_4_out, or_2_out, ring_counter_1_t4);
  and and_5 (and_5_out, not_1_out, or_4_out);
  or or_3 (mar_in_en, and_1_out, and_5_out);
  and and_6 (hlt, ins_dec_1_hlt, not_1_out, ring_counter_1_t4);
  or or_4 (or_4_out, and_4_out, ring_counter_1_t1);
  and and_7 (and_7_out, ins_dec_1_sta, not_1_out, ring_counter_1_t5);
  or or_5 (or_5_out, ins_dec_1_lda, ins_dec_1_ldb);
  and and_8 (and_8_out, or_5_out, ring_counter_1_t5);
  or or_6 (or_6_out, ins_dec_1_cmp, ins_dec_1_add, ins_dec_1_sub);
  and and_9 (and_9_out, or_6_out, ring_counter_1_t5);
  or or_7 (or_7_out, and_8_out, and_9_out, ring_counter_1_t2);
  and and_10 (sram_rd, or_7_out, not_1_out);
  and and_11 (pc_out, not_1_out, ring_counter_1_t1);
  and and_12 (pc_en, not_1_out, ring_counter_1_t3);
  and and_13 (pc_in, ring_counter_1_t5, not_1_out, ins_dec_1_jmp);
  and and_14 (ins_reg_in_en, not_1_out, ring_counter_1_t2);
  or or_8 (or_8_out, ins_dec_1_cmp, ins_dec_1_sub, ins_dec_1_add, ins_dec_1_ldb, ins_dec_1_lda, ins_dec_1_sta, ins_dec_1_jmp);
  and and_15 (and_15_out, or_8_out, ring_counter_1_t4);
  and and_16 (ins_reg_out_en, and_15_out, not_1_out);
  and and_17 (and_17_out, ring_counter_1_t5, ins_dec_1_lda);
  and and_18 (and_18_out, ins_dec_1_add, ring_counter_1_t6);
  or or_9 (or_9_out, and_17_out, and_18_out, and_20_out);
  and and_19 (a_in, not_1_out, or_9_out);
  and and_20 (and_20_out, ins_dec_1_sub, ring_counter_1_t6);
  and and_21 (and_21_out, ring_counter_1_t5, ins_dec_1_ldb);
  and and_22 (b_in, or_11_out, not_1_out);
  or or_10 (or_10_out, ins_dec_1_add, ins_dec_1_sub, ins_dec_1_cmp);
  and and_23 (and_23_out, or_10_out, ring_counter_1_t6);
  or or_11 (or_11_out, and_21_out, and_23_out);
  and and_24 (flag_in, not_1_out, and_29_out);
  or or_12 (or_12_out, ins_dec_1_cmp, ins_dec_1_sub);
  and and_25 (and_25_out, or_12_out, ring_counter_1_t6);
  and and_26 (alu_sub, not_1_out, and_25_out);
  or or_13 (or_13_out, ins_dec_1_add, ins_dec_1_sub);
  and and_27 (and_27_out, or_13_out, ring_counter_1_t6);
  and and_28 (alu_out, not_1_out, and_27_out);
  or or_14 (or_14_out, ins_dec_1_add, ins_dec_1_sub, ins_dec_1_cmp);
  and and_29 (and_29_out, or_14_out, ring_counter_1_t6);
endmodule

module ins_loader (
  input  bc_reset,
  input  bc_en,
  input  clk,
  input  debug,
  output [3:0] bc_address,
  output l1,
  output l2
);

  wire controlled_buffer_1_out, d_ff_1_q, not_1_out;

  Counter #(.max('hf), .width(4)) counter_1 (
    .clr(bc_reset), .load(1'b0), .up(1'b1), .count(bc_en), .clk(clk), .Q(bc_address));  // open: D, carry
  D_Flip_Flop d_ff_1 (.D(controlled_buffer_1_out), .clk(clk), .Q(d_ff_1_q));  // open: Qn, preset, reset
  assign controlled_buffer_1_out = debug ? not_1_out : 1'bz;  // Controlled_Buffer controlled_buffer_1
  not not_1 (not_1_out, d_ff_1_q);
  and and_1 (l1, debug, not_1_out);
  and and_2 (l2, debug, d_ff_1_q);
endmodule
